# Fritzing sketch WatchBot Model (saved by Fritzing 0.9.5d)
breadboards: 1

parts:
  Raspberry_pi_5 = Raspberry Pi 5
  Unknown_Person_Indicator = smd LED [color="Red (633nm)" package="0805 [SMD]"]
  R2 = Resistor [tolerance=±5% resistance=220 package="1206 [SMD]"]
  R3 = Resistor [tolerance=±5% resistance=220 package="1206 [SMD]"]
  LCD1 = LCD screen [part_number=Display]
  R4 = Resistor [tolerance=±5% resistance=1k package=THT]
  User_Related_Indicator = smd LED [color="Green (570nm)" package="0805 [SMD]"]
  R8 = Resistor [tolerance=±5% resistance=220 package=THT]
  Both_People = LED - 5mm [color="Yellow (592nm)" package="5 mm [THT]"]

nets:
  5V: Raspberry_pi_5.5V, LCD1.VDD, LCD1.LED+
  GND: Raspberry_pi_5.GND, Unknown_Person_Indicator.cathode, LCD1.VSS, LCD1.R/W, LCD1.LED-, R4.Pin_1, User_Related_Indicator.cathode, Both_People.anode
  N1: Raspberry_pi_5.GPIO15, R2.Pin_0
  N2: Raspberry_pi_5.GPIO18, R8.Pin_0
  N3: Raspberry_pi_5.GPIO24, LCD1.DB7
  N4: Raspberry_pi_5.GPIO25, LCD1.DB6
  N5: Raspberry_pi_5.GPIO8, LCD1.DB5
  N6: Raspberry_pi_5.GPIO7, LCD1.DB4
  N7: Raspberry_pi_5.GPIO5, LCD1.E
  N8: Unknown_Person_Indicator.anode, R2.Pin_1
  N9: R3.Pin_0, User_Related_Indicator.anode
  N10: LCD1.V0, R4.Pin_0
  N11: R8.Pin_1, Both_People.cathode

custom parts:
  Raspberry Pi 5: The RPi5, a faster version of the awesome Raspberry Pi4B ARM Board with 40 pin gpio.
